// Logisim project dcpu.circ as structural Verilog: 22 circuits, main circuit main
module main (
);

  wire dcpu_1_clk, dcpu_1_ramr, dcpu_1_ramw;
  wire [15:0] dcpu_1_addr, dcpu_1_dwrite, dcpu_1_pc, dcpu_1_sp, ram_1_data;

  // Probe on dcpu_1_pc
  // Probe on dcpu_1_sp
  DCPU dcpu_1 (
    .PC(dcpu_1_pc), .SP(dcpu_1_sp), .Dread(ram_1_data), .ramR(dcpu_1_ramr), .Dwrite(dcpu_1_dwrite),
    .ramW(dcpu_1_ramw), .Addr(dcpu_1_addr), .CLK(dcpu_1_clk));
  RAM #(.addrWidth(16), .dataWidth(16), .bus("separate")) ram_1 (
    .addr(dcpu_1_addr), .din(dcpu_1_dwrite), .data(ram_1_data), .str(dcpu_1_ramw), .clk(dcpu_1_clk),
    .ld(dcpu_1_ramr));  // open: sel, clr
endmodule

// instr fetch
module instruction_fetch (
  input  [15:0] data_in,
  input  [15:0] address_in,
  input  load,
  input  CLK,
  input  RST,
  output read,
  output [15:0] address_out,
  output [15:0] data_out
);

  assign address_out = load ? address_in : 16'bz;  // Controlled_Buffer controlled_buffer_1
  general_register REG (.Rin(data_in), .Rwr(load), .Rout(data_out), .CLK(CLK), .RST(RST));

  assign read = load;
endmodule

// decode
module instruction_decode (
  input  [15:0] instruction,
  output [3:0] op,
  output [5:0] argA,
  output [5:0] argB
);


  assign argA = instruction[9:4];
  assign argB = instruction[15:10];
  assign op = instruction[3:0];
endmodule

module alu (
  input  [3:0] operation,
  input  [15:0] Input_A,
  input  [15:0] Input_B,
  output [15:0] Output,
  output [15:0] Overflow
);

  wire [15:0] addOut, addOver, andOut, divOut, divOver, modOut, modOver, mulOut, mulOver, orOut, shlOut,
       shlOver, shrOut, shrOver, subOut, subOver, xorOut;

  // Probe on Input_A
  // Probe on Input_B
  add add_1 (.Input_A(Input_A), .Input_B(Input_B), .Output(addOut), .Overflow(addOver));
  sub sub_1 (.Input_A(Input_A), .Input_B(Input_B), .Output(subOut), .Overflow(subOver));
  mul mul_1 (.Input_A(Input_A), .Input_B(Input_B), .Output(mulOut), .Overflow(mulOver));
  div div_1 (.Input_A(Input_A), .Input_B(Input_B), .Output(divOut), .Overflow(divOver));
  mod mod_1 (.Input_A(Input_A), .Input_B(Input_B), .Output(modOut), .Overflow(modOver));
  shl shl_1 (.Input_A(Input_A), .Input_B(Input_B), .Output(shlOut), .Overflow(shlOver));
  shr shr_1 (.Input_A(Input_A), .Input_B(Input_B), .Output(shrOut), .Overflow(shrOver));
  assign andOut = Input_A & Input_B;  // AND_Gate and, 16 bits wide
  assign orOut = Input_A | Input_B;  // OR_Gate bor, 16 bits wide
  assign xorOut = Input_A ^ Input_B;  // XOR_Gate xor, 16 bits wide
  Multiplexer #(.select(4), .width(16), .enable("false")) multiplexer_1 (
    .in1(Input_B), .in2(addOut), .in3(subOut), .in4(mulOut), .in5(divOut), .in6(modOut), .in7(shlOut),
    .in8(shrOut), .in9(andOut), .in10(orOut), .in11(xorOut), .out(Output), .sel(operation));  // open: in0, in12, in13, in14, in15
  // Probe on Overflow
  Multiplexer #(.select(4), .width(16), .enable("false")) multiplexer_2 (
    .in2(addOver), .in3(subOver), .in4(mulOver), .in5(divOver), .in6(modOver), .in7(shlOver), .in8(shrOver),
    .in9(andOut), .in10(orOut), .in11(xorOut), .out(Overflow), .sel(operation));  // open: in0, in1, in12, in13, in14, in15
  // Probe on Output

  // Other names for the same wires on the sheet: A[15:0] = Input_A; B[15:0] = Input_B; OP[3:0] = operation
endmodule

module add (
  input  [15:0] Input_A,
  input  [15:0] Input_B,
  output [15:0] Output,
  output [15:0] Overflow
);

  wire adder_1_cout;

  Adder #(.width(16)) adder_1 (.a(Input_A), .b(Input_B), .out(Output), .cout(adder_1_cout));  // open: cin
  Multiplexer #(.width(16), .enable("false")) multiplexer_1 (
    .in0({16{1'b0}}), .in1(16'h1), .out(Overflow), .sel(adder_1_cout));
endmodule

module sub (
  input  [15:0] Input_A,
  input  [15:0] Input_B,
  output [15:0] Output,
  output [15:0] Overflow
);

  wire subtractor_1_bout;

  Subtractor #(.width(16)) subtractor_1 (
    .a(Input_A), .b(Input_B), .out(Output), .bout(subtractor_1_bout));  // open: bin
  Multiplexer #(.width(16), .enable("false")) multiplexer_1 (
    .in0({16{1'b0}}), .in1({16{1'b1}}), .out(Overflow), .sel(subtractor_1_bout));
endmodule

module mul (
  input  [15:0] Input_A,
  input  [15:0] Input_B,
  output [15:0] Output,
  output [15:0] Overflow
);

  Multiplier #(.width(16)) multiplier_1 (.a(Input_A), .b(Input_B), .out(Output), .cout(Overflow));  // open: cin
endmodule

module div (
  input  [15:0] Input_A,
  input  [15:0] Input_B,
  output [15:0] Output,
  output [15:0] Overflow
);

  wire comparator_1_eq;
  wire [15:0] divider_1_out, divider_2_out;

  Divider #(.width(16)) divider_1 (.a(Input_A), .b(Input_B), .out(divider_1_out));  // open: upper, rem
  Comparator #(.width(16), .mode("unsigned")) comparator_1 (
    .a(Input_B), .b({16{1'b0}}), .eq(comparator_1_eq));  // open: gt, lt
  Divider #(.width(16)) divider_2 (.a({16{1'b0}}), .b(Input_B), .out(divider_2_out), .upper(Input_A));  // open: rem
  Multiplexer #(.width(16), .enable("false")) multiplexer_1 (
    .in0(divider_1_out), .in1(Overflow), .out(Output), .sel(comparator_1_eq));
  Multiplexer #(.width(16), .enable("false")) multiplexer_2 (
    .in0(divider_2_out), .in1({16{1'b0}}), .out(Overflow), .sel(comparator_1_eq));
endmodule

module mod (
  input  [15:0] Input_A,
  input  [15:0] Input_B,
  output [15:0] Output,
  output [15:0] Overflow
);

  wire comparator_1_eq;
  wire [15:0] divider_1_rem;

  Divider #(.width(16)) divider_1 (.a(Input_A), .b(Input_B), .rem(divider_1_rem));  // open: out, upper
  Comparator #(.width(16), .mode("unsigned")) comparator_1 (
    .a(Input_B), .b({16{1'b0}}), .eq(comparator_1_eq));  // open: gt, lt
  Multiplexer #(.width(16), .enable("false")) multiplexer_1 (
    .in0(divider_1_rem), .in1({16{1'b0}}), .out(Output), .sel(comparator_1_eq));

  assign Overflow = {16{1'b0}};
endmodule

module shl (
  input  [15:0] Input_A,
  input  [15:0] Input_B,
  output [15:0] Output,
  output [15:0] Overflow
);

  wire comparator_1_gt;
  wire [31:0] shifter_1_out;

  Shifter #(.width(32)) shifter_1 (.in({{16{1'b0}}, Input_A}), .\dist (Input_B[4:0]), .out(shifter_1_out));
  Comparator #(.width(16), .mode("unsigned")) comparator_1 (
    .a(Input_B), .b(16'h1f), .gt(comparator_1_gt));  // open: eq, lt
  Multiplexer #(.width(32), .enable("false")) multiplexer_1 (
    .in0(shifter_1_out), .in1({32{1'b0}}), .out({Overflow, Output}), .sel(comparator_1_gt));
endmodule

module shr (
  input  [15:0] Input_A,
  input  [15:0] Input_B,
  output [15:0] Output,
  output [15:0] Overflow
);

  wire [1:0] comparator_1_gt;
  wire [15:0] shifter_2_out;
  wire [31:0] shifter_1_out;

  Shifter #(.width(32), .shift("rr")) shifter_1 (
    .in({{16{1'b0}}, Input_A}), .\dist (Input_B[4:0]), .out(shifter_1_out));
  Shifter #(.width(16), .shift("lr")) shifter_2 (.in(Input_A), .\dist (Input_B[3:0]), .out(shifter_2_out));
  Comparator #(.width(16), .mode("unsigned")) comparator_1 (
    .a(Input_B), .b(16'h10), .gt(comparator_1_gt[0]));  // open: eq, lt
  Comparator #(.width(16), .mode("unsigned")) comparator_2 (
    .a(Input_B), .b(16'h1f), .gt(comparator_1_gt[1]));  // open: eq, lt
  Multiplexer #(.select(2), .width(32), .enable("false")) multiplexer_1 (
    .in0(shifter_1_out), .in1({shifter_2_out, {16{1'b0}}}), .in3({32{1'b0}}), .out({Overflow, Output}),
    .sel(comparator_1_gt));  // open: in2
endmodule

module ifx (
  input  [3:0] op,
  input  [15:0] PCin,
  input  [15:0] Input_A,
  input  [15:0] Input_B,
  output [15:0] PCout
);

  wire comparator_1_eq, comparator_1_gt, comparator_2_eq, not_1_out, not_2_out, not_3_out, subtractor_1_bout;
  wire [1:0] bit_extender_5_out;
  wire [3:0] subtractor_1_out;
  wire [15:0] adder_1_out, adder_2_out, adder_3_out, adder_4_out, and_1_out, bit_extender_1_out,
       bit_extender_2_out, bit_extender_3_out, bit_extender_4_out;

  assign and_1_out = Input_A & Input_B;  // AND_Gate and_1, 16 bits wide
  Comparator #(.width(16), .mode("unsigned")) comparator_1 (
    .a(Input_A), .b(Input_B), .gt(comparator_1_gt), .eq(comparator_1_eq));  // open: lt
  Comparator #(.width(16), .mode("unsigned")) comparator_2 (
    .a(and_1_out), .b({16{1'b0}}), .eq(comparator_2_eq));  // open: gt, lt
  not not_1 (not_1_out, comparator_1_eq);
  not not_2 (not_2_out, comparator_2_eq);
  assign bit_extender_1_out = {{15{1'b0}}, comparator_1_gt};  // Bit_Extender bit_extender_1
  assign bit_extender_2_out = {{15{1'b0}}, comparator_1_eq};  // Bit_Extender bit_extender_2
  assign bit_extender_3_out = {{15{1'b0}}, not_1_out};  // Bit_Extender bit_extender_3
  assign bit_extender_4_out = {{15{1'b0}}, not_2_out};  // Bit_Extender bit_extender_4
  Adder #(.width(16)) adder_1 (.a(PCin), .b(bit_extender_1_out), .out(adder_1_out), .cin(1'b1));  // open: cout
  Adder #(.width(16)) adder_2 (.a(PCin), .b(bit_extender_2_out), .out(adder_2_out), .cin(1'b1));  // open: cout
  Adder #(.width(16)) adder_3 (.a(PCin), .b(bit_extender_3_out), .out(adder_3_out), .cin(1'b1));  // open: cout
  Adder #(.width(16)) adder_4 (.a(PCin), .b(bit_extender_4_out), .out(adder_4_out), .cin(1'b1));  // open: cout
  Subtractor #(.width(4)) subtractor_1 (
    .a(op), .b(4'b1100), .out(subtractor_1_out), .bout(subtractor_1_bout));  // open: bin
  // Probe on bit_extender_5_out
  not not_3 (not_3_out, subtractor_1_bout);
  Multiplexer #(.select(2), .width(16)) multiplexer_1 (
    .in0(adder_1_out), .in1(adder_2_out), .in2(adder_3_out), .in3(adder_4_out), .out(PCout),
    .sel(bit_extender_5_out), .en(not_3_out));
  Bit_Extender #(.in_width(4), .out_width(2)) bit_extender_5 (.in(subtractor_1_out), .out(bit_extender_5_out));

  // Other names for the same wires on the sheet: A[15:0] = Input_A; B[15:0] = Input_B
endmodule

module general_register (
  input  [15:0] Rin,
  input  Rwr,
  input  CLK,
  input  RST,
  output [15:0] Rout
);

  Register #(.width(16)) register (.D(Rin), .en(Rwr), .Q(Rout), .clk(CLK), .clr(RST));
endmodule

module PC (
  input  [15:0] PCin,
  input  PCwr,
  input  CLK,
  input  RST,
  output [15:0] PCout
);

  wire not_1_out;

  not not_1 (not_1_out, PCwr);
  // Probe on PCout
  Counter #(.width(16), .max('hffff)) PC (
    .load(PCwr), .D(PCin), .count(not_1_out), .Q(PCout), .clk(CLK), .clr(RST));  // open: carry
endmodule

module SP (
  input  SPdec,
  input  SPinc,
  input  [15:0] SPin,
  input  SPwr,
  input  CLK,
  input  RST,
  output [15:0] SPout
);

  wire or_1_out, priority_encoder_1_gs, t_ff_1_q;
  wire [1:0] priority_encoder_1_out;
  wire [15:0] adder_1_out, multiplexer_1_out, subtractor_1_out;

  Adder #(.width(16)) adder_1 (.a(SPout), .b(16'h1), .out(adder_1_out));  // open: cin, cout
  Subtractor #(.width(16)) subtractor_1 (.a(SPout), .b(16'h1), .out(subtractor_1_out));  // open: bin, bout
  Multiplexer #(.select(2), .width(16)) multiplexer_1 (
    .in1(SPin), .in2(adder_1_out), .in3(subtractor_1_out), .out(multiplexer_1_out),
    .sel(priority_encoder_1_out), .en(priority_encoder_1_gs));  // open: in0
  Priority_Encoder #(.select(2)) priority_encoder_1 (
    .in1(SPwr), .in2(SPinc), .in3(SPdec), .out(priority_encoder_1_out), .gs(priority_encoder_1_gs));  // open: in0, en_out, en_in
  T_Flip_Flop t_ff_1 (.clk(SPdec), .T(1'b1), .Q(t_ff_1_q), .reset(CLK), .en(1'b1));  // open: Qn, preset
  // Probe on multiplexer_1_out
  Register #(.width(16)) SP (.D(multiplexer_1_out), .en(priority_encoder_1_gs), .Q(SPout), .clk(or_1_out), .clr(RST));
  or or_1 (or_1_out, t_ff_1_q, CLK);
  // Probe on SPout
endmodule

module DCPU (
  input  [15:0] Dread,
  output [15:0] PC,
  output [15:0] SP,
  output ramR,
  output [15:0] Dwrite,
  output ramW,
  output [15:0] Addr,
  output CLK
);

  wire Aen, and_1_out, and_2_out, Ben, buffer_2_out, buffer_3_out, Cen, CLK_t, comparator_1_eq,
       comparator_2_eq, data_fetch_1_read, data_fetch_1_regdest, DFetch, DFready, done, exec, Ien, IFetch,
       instruction_fetch_1_read, Jen, Oen, or_1_out, or_3_out, PCen, pull_resistor_1_node,
       pull_resistor_3_node, regW, RST, SPen, Xen, Yen, Zen;
  wire [1:0] data_fetch_1_cycles, data_fetch_1_pcinc, data_fetch_1_spdec, data_fetch_1_spinc;
  wire [3:0] data_fetch_1_reg, data_fetch_1_regsela, data_fetch_1_regselb, op, regSel;
  wire [5:0] argA, instruction_decode_1_argb;
  wire [15:0] A, addr_t, Ain, B, Bin, C, Cin, data_fetch_1_dest, data_fetch_1_vala, data_fetch_1_valb, I,
       Iin, instruction_fetch_1_address_out, instruction_fetch_1_data_out, J, Jin, multiplexer_2_out,
       multiplexer_3_out, O, Oin, PCin, PCout, reg_data_fetch_1_dout, reg_data_fetch_2_dout, regData, SPin,
       SPout, X, Xin, Y, Yin, Z, Zin;

  Pull_Resistor #(.pull(1)) pull_resistor_1 (.node(pull_resistor_1_node));
  Multiplexer #(.width(16), .enable("false")) multiplexer_1 (
    .in0(instruction_fetch_1_address_out), .in1(addr_t), .out(Addr), .sel(ramW));
  // Probe on instruction_fetch_1_address_out
  // Probe on PC
  Comparator #(.width(4), .mode("unsigned")) comparator_1 (
    .a(regSel), .b(4'b1001), .eq(comparator_1_eq));  // open: gt, lt
  buf buffer_1 (pull_resistor_1_node, comparator_1_eq);
  and and_1 (and_1_out, pull_resistor_1_node, regW);
  instruction_fetch instruction_fetch_1 (
    .address_in(PC), .load(IFetch), .address_out(instruction_fetch_1_address_out),
    .read(instruction_fetch_1_read), .data_in(Dread), .CLK(CLK_t), .RST(RST),
    .data_out(instruction_fetch_1_data_out));
  Button button_1 (.out(RST));
  T_Flip_Flop t_ff_1 (.clk(CLK), .T(1'b1), .Q(CLK_t), .en(1'b1));  // open: Qn, preset, reset
  buf buffer_2 (buffer_2_out, comparator_1_eq);
  Pull_Resistor pull_resistor_2 (.node(buffer_2_out));
  // Probe on multiplexer_2_out
  Multiplexer #(.width(16), .enable("false")) multiplexer_2 (
    .in0(PCout), .in1(PCin), .out(multiplexer_2_out), .sel(buffer_2_out));
  or or_1 (or_1_out, and_1_out, done);
  or or_2 (ramR, instruction_fetch_1_read, data_fetch_1_read);
  // Probe on instruction_fetch_1_data_out
  instruction_decode instruction_decode_1 (
    .instruction(instruction_fetch_1_data_out), .op(op), .argA(argA), .argB(instruction_decode_1_argb));
  // Probe on argA
  // Probe on instruction_decode_1_argb
  Register #(.width(16)) register_1 (.D(multiplexer_2_out), .en(or_1_out), .Q(PC), .clk(CLK), .clr(RST));
  // Probe on Dread
  // Probe on op
  Pull_Resistor #(.pull(1)) pull_resistor_3 (.node(pull_resistor_3_node));
  // Probe on data_fetch_1_regsela
  // Probe on data_fetch_1_regdest
  // Probe on data_fetch_1_reg
  // Probe on data_fetch_1_dest
  Comparator #(.width(4), .mode("unsigned")) comparator_2 (
    .a(regSel), .b(4'b1000), .eq(comparator_2_eq));  // open: gt, lt
  buf buffer_3 (buffer_3_out, comparator_2_eq);
  buf buffer_4 (pull_resistor_3_node, comparator_2_eq);
  and and_2 (and_2_out, pull_resistor_3_node, regW);
  data_fetch data_fetch_1 (
    .PCin(PC), .op(op), .argA(argA), .argB(instruction_decode_1_argb), .load(DFetch),
    .regSelA(data_fetch_1_regsela), .regAIn(reg_data_fetch_1_dout), .regSelB(data_fetch_1_regselb),
    .regBIn(reg_data_fetch_2_dout), .address(instruction_fetch_1_address_out), .ramIn(Dread),
    .read(data_fetch_1_read), .regDest(data_fetch_1_regdest), .\reg (data_fetch_1_reg),
    .dest(data_fetch_1_dest), .CLK(CLK_t), .RST(RST), .cycles(data_fetch_1_cycles),
    .PCinc(data_fetch_1_pcinc), .SPinc(data_fetch_1_spinc), .SPdec(data_fetch_1_spdec), .done(DFready),
    .valA(data_fetch_1_vala), .valB(data_fetch_1_valb));
  Pull_Resistor pull_resistor_4 (.node(buffer_3_out));
  Multiplexer #(.width(16), .enable("false")) multiplexer_3 (
    .in0(SPout), .in1(SPin), .out(multiplexer_3_out), .sel(buffer_3_out));
  Register #(.width(16)) register_2 (.D(multiplexer_3_out), .en(or_3_out), .Q(SP), .clk(CLK), .clr(RST));
  or or_3 (or_3_out, and_2_out, done);
  reg_data_fetch reg_data_fetch_1 (
    .regSel(data_fetch_1_regsela), .load(1'b1), .A(A), .B(B), .C(C), .X(X), .Y(Y), .Z(Z), .I(I), .J(J),
    .SP(SP), .PC(PC), .O(O), .dOut(reg_data_fetch_1_dout));
  // Probe on reg_data_fetch_1_dout
  // Probe on data_fetch_1_cycles
  // Probe on data_fetch_1_pcinc
  // Probe on data_fetch_1_spinc
  // Probe on data_fetch_1_spdec
  // Probe on data_fetch_1_regselb
  // Probe on data_fetch_1_valb
  // Probe on data_fetch_1_vala
  // Probe on DFready
  control control_1 (.DFready(DFready), .EXready(done), .CLK(CLK_t), .RST(RST), .IF(IFetch), .DF(DFetch), .EX(exec));
  reg_data_fetch reg_data_fetch_2 (
    .regSel(data_fetch_1_regselb), .load(1'b1), .A(A), .B(B), .C(C), .X(X), .Y(Y), .Z(Z), .I(I), .J(J),
    .SP(SP), .PC(PC), .O(O), .dOut(reg_data_fetch_2_dout));
  // Probe on reg_data_fetch_2_dout
  Register #(.width(16)) register_3 (.D(Ain), .en(Aen), .Q(A), .clk(CLK), .clr(RST));
  Register #(.width(16)) register_4 (.D(Xin), .en(Xen), .Q(X), .clk(CLK), .clr(RST));
  Register #(.width(16)) register_5 (.D(Iin), .en(Ien), .Q(I), .clk(CLK), .clr(RST));
  // Probe on SPout
  // Probe on PCout
  Register #(.width(16)) register_6 (.D(Bin), .en(Ben), .Q(B), .clk(CLK), .clr(RST));
  Register #(.width(16)) register_7 (.D(Yin), .en(Yen), .Q(Y), .clk(CLK), .clr(RST));
  Register #(.width(16)) register_8 (.D(Jin), .en(Jen), .Q(J), .clk(CLK), .clr(RST));
  exec exec_1 (
    .argA(argA), .op(op), .valA(data_fetch_1_vala), .valB(data_fetch_1_valb), .load(exec),
    .regDest(data_fetch_1_regdest), .\reg (data_fetch_1_reg), .dest(data_fetch_1_dest), .PCin(PC),
    .PCinc(data_fetch_1_pcinc), .SPin(SP), .SPinc(data_fetch_1_spinc), .SPDec(data_fetch_1_spdec),
    .SPOut(SPout), .PCOut(PCout), .CLK(CLK_t), .RST(RST), .address(addr_t), .ramOut(Dwrite), .ramW(ramW),
    .regSel(regSel), .regOut(regData), .regW(regW), .done(done));
  Register #(.width(16)) register_9 (.D(Cin), .en(Cen), .Q(C), .clk(CLK), .clr(RST));
  Register #(.width(16)) register_10 (.D(Zin), .en(Zen), .Q(Z), .clk(CLK), .clr(RST));
  Register #(.width(16)) register_11 (.D(Oin), .en(Oen), .Q(O), .clk(CLK), .clr(RST));
  // Probe on addr_t
  // Probe on Dwrite
  // Probe on regSel
  // Probe on regData
  reg_data_put reg_data_put_1 (
    .regSel(regSel), .Data_In(regData), .load(regW), .A(Ain), .Awr(Aen), .B(Bin), .Bwr(Ben), .C(Cin),
    .Cwr(Cen), .X(Xin), .Cwr_2(Xen), .Y(Yin), .Ywr(Yen), .Z(Zin), .Zwr(Zen), .I(Iin), .Iwr(Ien), .J(Jin),
    .Jwr(Jen), .SP(SPin), .SPwr(SPen), .PC(PCin), .PCwr(PCen), .O(Oin), .Owr(Oen));
  RAM #(.addrWidth(16), .dataWidth(16), .bus("separate")) ram_1 ();  // open: addr, din, data, str, sel, clk, ld, clr
  Clock clock_1 (.out(CLK));

  // Other names for the same wires on the sheet: address[15:0] = Addr; CLK2 = CLK; data[15:0] = Dwrite
endmodule

// reg fetch
module reg_data_fetch (
  input  [15:0] A,
  input  [15:0] B,
  input  [15:0] C,
  input  [15:0] X,
  input  [15:0] Y,
  input  [15:0] Z,
  input  [15:0] I,
  input  [15:0] J,
  input  [15:0] SP,
  input  [15:0] PC,
  input  [15:0] O,
  input  [3:0] regSel,
  input  load,
  output [15:0] dOut
);

  Multiplexer #(.select(4), .width(16)) multiplexer_1 (
    .in0(A), .in1(B), .in2(C), .in3(X), .in4(Y), .in5(Z), .in6(I), .in7(J), .in8(SP), .in9(PC), .in10(O),
    .out(dOut), .sel(regSel), .en(load));  // open: in11, in12, in13, in14, in15
endmodule

// fetch
module data_fetch (
  input  [15:0] regAIn,
  input  [15:0] regBIn,
  input  [15:0] ramIn,
  input  [15:0] PCin,
  input  [3:0] op,
  input  [5:0] argA,
  input  [5:0] argB,
  input  load,
  input  RST,
  input  CLK,
  output [3:0] regSelA,
  output [3:0] regSelB,
  output [15:0] address,
  output read,
  output [1:0] cycles,
  output [1:0] PCinc,
  output [1:0] SPinc,
  output [1:0] SPdec,
  output done,
  output [15:0] valA,
  output [15:0] valB,
  output [15:0] dest,
  output regDest,
  output [3:0] \reg 
);

  wire addr_NWregA, addr_NWregB, addr_regA, addr_regB, and_1_out, and_2_out, and_3_out, and_4_out, and_5_out,
       button_1_out, channel, CLK_t, controlled_buffer_3_out, loadA, loadB, memA, memB, NWandA, NWandB,
       or_1_out, or_2_out, or_3_out, or_6_out, or_7_out, PCincA, PCincB, regA_read, regB, regB_read, setsO,
       SPdecA, SPdecB, SPincA, SPincB, valA_dataIn, valA_regA, valB_dataIn, valB_immB, valB_regB;
  wire [1:0] bitadder_2_out, bitadder_3_out, phase, phases, priority_encoder_2_out, priority_encoder_3_out;
  wire [2:0] bitadder_1_out;
  wire [4:4] immA, immB;
  wire [7:3] rom_1_data;
  wire [15:0] adder_1_out, adder_2_out, adder_3_out, adder_5_out, adder_6_out, addrA, addrB,
       bit_extender_1_out, bit_extender_2_out, bit_extender_3_out, demultiplexer_2_out1,
       demultiplexer_2_out2, demultiplexer_2_out3, demultiplexer_3_out1, demultiplexer_3_out2,
       demultiplexer_3_out3, multiplexer_4_out, multiplexer_6_out, ramInA, ramInB, register_1_q,
       subtractor_1_out, subtractor_2_out, valA_t, valB_t;
  wire [15:10] rom_4_data;
  wire [15:11] rom_2_data, rom_3_data;

  // Probe on regAIn
  // Probe on PCin
  // Probe on argA
  // Probe on argB
  // Probe on {memA, regDest, NWandA, memB, regB, NWandB, phase}
  and and_1 (and_1_out, load, ~done);  // AND_Gate
  Counter #(.width(2), .max('h3)) counter_1 (
    .count(and_1_out), .Q(phase), .clk(CLK_t), .clr(or_1_out));  // open: load, D, carry
  // Probe on regBIn
  or or_1 (or_1_out, RST, and_2_out);
  // Probe on {rom_1_data, cycles, setsO}
  ROM #(.addrWidth(4)) rom_1 (.addr(op), .data({rom_1_data, cycles, setsO}));  // open: sel
  ROM #(.addrWidth(6), .dataWidth(16)) rom_2 (
    .addr(argA), .data({rom_2_data, memA, regDest, NWandA, SPdecA, SPincA, PCincA, immA[4], regSelA}));  // open: sel
  ROM #(.addrWidth(6), .dataWidth(16)) rom_3 (
    .addr(argB), .data({rom_3_data, memB, regB, NWandB, SPdecB, SPincB, PCincB, immB[4], regSelB}));  // open: sel
  ROM #(.dataWidth(16)) rom_4 (
    .addr({memA, regDest, NWandA, memB, regB, NWandB, phase}),
    .data({rom_4_data, valA_regA, addr_regA, addr_NWregA, valA_dataIn, valB_immB, valB_regB, addr_regB, addr_NWregB, valB_dataIn, done}));  // open: sel
  and and_2 (and_2_out, CLK_t, ~load, done);  // AND_Gate
  assign \reg  = regDest ? regSelA : 4'bz;  // Controlled_Buffer controlled_buffer_1
  // Probe on ramIn
  Multiplexer #(.width(16)) multiplexer_1 (.in0(addrA), .in1(addrB), .out(address), .sel(channel), .en(read));
  // Probe on cycles
  Priority_Encoder #(.select(1)) priority_encoder_1 (
    .in0(valA_dataIn), .in1(valB_dataIn), .out(channel), .gs(read));  // open: en_out, en_in
  Demultiplexer #(.width(16)) demultiplexer_1 (.out0(ramInA), .out1(ramInB), .in(ramIn), .sel(channel), .en(read));
  and and_3 (and_3_out, SPincB, SPincA);
  and and_4 (and_4_out, PCincB, PCincA);
  BitAdder #(.width(1)) bitadder_1 (.in0(SPincB), .in1(and_3_out), .in2(PCincB), .in3(and_4_out), .out(bitadder_1_out));
  assign bit_extender_1_out = {{13{1'b0}}, bitadder_1_out};  // Bit_Extender bit_extender_1
  Adder #(.width(16)) adder_1 (.a(regAIn), .b({16{1'b0}}), .out(adder_1_out), .cin(SPincA));  // open: cout
  Subtractor #(.width(16)) subtractor_1 (
    .a(adder_1_out), .b({16{1'b0}}), .out(subtractor_1_out), .bin(SPdecA));  // open: bout
  Adder #(.width(16)) adder_2 (.a(regBIn), .b(bit_extender_1_out), .out(adder_2_out));  // open: cin, cout
  and and_5 (and_5_out, SPdecB, SPdecA);
  or or_2 (or_2_out, addr_regA, addr_NWregA);
  // Probe on adder_3_out
  // Probe on subtractor_1_out
  Adder #(.width(16)) adder_3 (.a(subtractor_1_out), .b({16{1'b0}}), .out(adder_3_out), .cin(PCincA));  // open: cout
  // Probe on adder_3_out
  BitAdder #(.width(1)) bitadder_2 (.in0(SPdecB), .in1(and_5_out), .out(bitadder_2_out));
  assign bit_extender_2_out = {{14{1'b0}}, bitadder_2_out};  // Bit_Extender bit_extender_2
  Register #(.width(16)) register_1 (.D(addrA), .en(or_2_out), .Q(register_1_q), .clk(CLK_t), .clr(RST));
  assign dest = memA ? register_1_q : 16'bz;  // Controlled_Buffer controlled_buffer_2
  BitAdder #(.width(1)) bitadder_3 (.in0(memA), .in1(memB), .out(bitadder_3_out));
  Adder #(.width(2)) adder_4 (.a(bitadder_3_out), .b(2'b01), .out(phases));  // open: cin, cout
  Priority_Encoder #(.select(2)) priority_encoder_2 (
    .in1(valA_regA), .in2(addr_regA), .in3(addr_NWregA), .out(priority_encoder_2_out), .gs(regA_read));  // open: in0, en_out, en_in
  Demultiplexer #(.select(2), .width(16)) demultiplexer_2 (
    .out1(demultiplexer_2_out1), .out2(demultiplexer_2_out2), .out3(demultiplexer_2_out3), .in(adder_3_out),
    .sel(priority_encoder_2_out), .en(regA_read));  // open: out0
  Subtractor #(.width(16)) subtractor_2 (
    .a(adder_2_out), .b(bit_extender_2_out), .out(subtractor_2_out));  // open: bin, bout
  Adder #(.width(16)) adder_5 (.a(demultiplexer_2_out3), .b(PCin), .out(adder_5_out));  // open: cin, cout
  assign bit_extender_3_out = {{11{1'b0}}, {immB[4], regSelB}};  // Bit_Extender bit_extender_3
  or or_3 (or_3_out, addr_regA, addr_NWregA);
  Multiplexer #(.width(16)) multiplexer_2 (
    .in0(demultiplexer_2_out2), .in1(adder_5_out), .out(addrA), .sel(addr_NWregA), .en(or_3_out));
  or or_4 (loadA, valA_dataIn, valA_regA);
  Multiplexer #(.width(16)) multiplexer_3 (
    .in0(demultiplexer_2_out1), .in1(ramInA), .out(valA_t), .sel(valA_dataIn), .en(loadA));
  // Probe on valA_t
  Multiplexer #(.width(16), .enable("false")) multiplexer_4 (
    .in0(subtractor_2_out), .in1(bit_extender_3_out), .out(multiplexer_4_out), .sel(valB_immB));
  // Probe on multiplexer_4_out
  // Probe on addrA
  Priority_Encoder #(.select(2)) priority_encoder_3 (
    .in1(valB_regB), .in2(addr_regB), .in3(addr_NWregB), .out(priority_encoder_3_out), .gs(regB_read));  // open: in0, en_out, en_in
  Demultiplexer #(.select(2), .width(16)) demultiplexer_3 (
    .out1(demultiplexer_3_out1), .out2(demultiplexer_3_out2), .out3(demultiplexer_3_out3),
    .in(multiplexer_4_out), .sel(priority_encoder_3_out), .en(regB_read));  // open: out0
  // Probe on valA_t
  // Probe on valB_t
  Adder #(.width(16)) adder_6 (.a(demultiplexer_3_out3), .b(PCin), .out(adder_6_out));  // open: cin, cout
  assign controlled_buffer_3_out = load ? CLK_t : 1'bz;  // Controlled_Buffer controlled_buffer_3
  or or_5 (CLK_t, button_1_out, CLK);
  Button button_1 (.out(button_1_out));
  or or_6 (or_6_out, addr_regB, addr_NWregB);
  Multiplexer #(.width(16)) multiplexer_5 (
    .in0(demultiplexer_3_out2), .in1(adder_6_out), .out(addrB), .sel(addr_NWregB), .en(or_6_out));
  or or_7 (or_7_out, valB_dataIn, valB_regB);
  Multiplexer #(.width(16)) multiplexer_6 (
    .in0(demultiplexer_3_out1), .in1(ramInB), .out(multiplexer_6_out), .sel(valB_dataIn), .en(or_7_out));
  Multiplexer #(.width(16), .enable("false")) multiplexer_7 (
    .in0(multiplexer_6_out), .in1(multiplexer_4_out), .out(valB_t), .sel(valB_immB));
  Adder #(.width(1)) adder_7 (.a(PCincA), .b(PCincB), .out(PCinc[0]), .cin(1'b1), .cout(PCinc[1]));
  BitAdder #(.width(1)) bitadder_4 (.in0(SPincA), .in1(SPincB), .out(SPinc));
  BitAdder #(.width(1)) bitadder_5 (.in0(SPdecA), .in1(SPdecB), .out(SPdec));
  Register #(.width(16)) register_2 (.D(valA_t), .en(loadA), .Q(valA), .clk(controlled_buffer_3_out), .clr(RST));
  Register #(.width(16)) register_3 (.D(valB_t), .en(loadB), .Q(valB), .clk(controlled_buffer_3_out), .clr(RST));
  or or_8 (loadB, or_7_out, valB_immB);

  // Other names for the same wires on the sheet: immA[3:0] = regSelA; rsA[3:0] = regSelA; regA = regDest;
  //   immB[3:0] = regSelB; rsB[3:0] = regSelB; opcycles[1:0] = cycles; regInA[15:0] = regAIn; regInB[15:0] = regBIn

  // Notes on the sheet:
  //   contents of rom_1 (hex, n*v repeats v):
  //   4 6 5 5 5 7 6 5 5 4 4 4 4*6
  //   contents of rom_2 (hex, n*v repeats v):
  //   200 201 202 203 204 205 206 207 400 401 402 403 404 405 406 407 520 521 522 523 524 525 526 527 448
  //   408 488 208 209 20a 429 229 0 1 2 3 4 5 6 7 8 9 a b c d e f 10 11 12 13 14 15 16 17 18 19 1a 1b 1c
  //   1d 1e 1f
  //   contents of rom_3 (hex, n*v repeats v):
  //   200 201 202 203 204 205 206 207 400 401 402 403 404 405 406 407 520 521 522 523 524 525 526 527 448
  //   408 488 208 209 20a 429 229 0 1 2 3 4 5 6 7 8 9 a b c d e f 10 11 12 13 14 15 16 17 18 19 1a 1b 1c
  //   1d 1e 1f
  //   contents of rom_4 (hex, n*v repeats v):
  //   64*0 220 1 6*0 210 1 6*0 208 1 0 0 204 6 1 41*0 120 140 1 5*0 110 140 1 5*0 100 148 a 1 100 144 6 1
  //   8*0 a0 c0 1 5*0 90 c0 1 5*0 80 c8 a 1 80 c4 6 1
endmodule

module exec (
  input  [15:0] PCin,
  input  [1:0] PCinc,
  input  [15:0] SPin,
  input  [1:0] SPinc,
  input  [1:0] SPDec,
  input  [5:0] argA,
  input  [3:0] op,
  input  [15:0] valA,
  input  [15:0] valB,
  input  load,
  input  regDest,
  input  [3:0] \reg ,
  input  [15:0] dest,
  input  CLK,
  input  RST,
  output [15:0] SPOut,
  output [15:0] PCOut,
  output [15:0] address,
  output [15:0] ramOut,
  output ramW,
  output [3:0] regSel,
  output [15:0] regOut,
  output regW,
  output done
);

  wire button_1_out, CLK_t, comparator_1_gt, comparator_2_eq, comparator_3_eq, comparator_4_gt,
       comparator_4_lt, comparator_5_gt, comparator_5_lt, jsr, or_1_out, or_2_out, ramS, ramW_t, regW_t,
       RST_t;
  wire [1:0] phase, priority_encoder_1_out, regS;
  wire [3:0] setAregSel;
  wire [15:0] aluOut, bit_extender_1_out, bit_extender_2_out, bit_extender_3_out, ifxOut, overflow, PCnext,
       register_1_q, register_2_q, setAaddr, setAramOut, setAregOut, setPCregOut, setSPregOut, SPnext,
       subtractor_1_out, subtractor_2_out;

  ifx ifx_1 (.Input_A(valA), .Input_B(valB), .op(op), .PCin(PCnext), .PCout(ifxOut));
  // Probe on valA
  // Probe on valB
  assign bit_extender_1_out = {{14{1'b0}}, SPDec};  // Bit_Extender bit_extender_1
  alu alu_1 (.operation(op), .Input_A(valA), .Input_B(valB), .Output(aluOut), .Overflow(overflow));
  Subtractor #(.width(16)) subtractor_1 (.a(SPin), .b(bit_extender_1_out), .out(subtractor_1_out));  // open: bin, bout
  assign bit_extender_2_out = {{14{1'b0}}, SPinc};  // Bit_Extender bit_extender_2
  // Probe on PCnext
  assign bit_extender_3_out = {{14{1'b0}}, PCinc};  // Bit_Extender bit_extender_3
  // Probe on SPnext
  Adder #(.width(16)) adder_1 (.a(subtractor_1_out), .b(bit_extender_2_out), .out(SPnext));  // open: cin, cout
  Adder #(.width(16)) adder_2 (.a(PCin), .b(bit_extender_3_out), .out(PCnext));  // open: cin, cout
  Comparator #(.width(4), .mode("unsigned")) comparator_1 (.a(op), .b(4'b1011), .gt(comparator_1_gt));  // open: eq, lt
  Comparator #(.width(4), .mode("unsigned")) comparator_2 (.a(op), .b(4'b0000), .eq(comparator_2_eq));  // open: gt, lt
  and and_1 (jsr, comparator_2_eq, comparator_3_eq);
  Comparator #(.width(6), .mode("unsigned")) comparator_3 (
    .a(argA), .b(6'b000001), .eq(comparator_3_eq));  // open: gt, lt
  Subtractor #(.width(16)) subtractor_2 (.a(SPnext), .b(16'h1), .out(subtractor_2_out));  // open: bin, bout
  Demultiplexer #(.width(16), .enable("false")) demultiplexer_1 (
    .out0(setAramOut), .out1(setAregOut), .in(aluOut), .sel(regDest));
  Multiplexer #(.width(4), .enable("false")) multiplexer_1 (.in1(\reg ), .out(setAregSel), .sel(regDest));  // open: in0
  Multiplexer #(.width(16), .enable("false")) multiplexer_2 (.in0(dest), .out(setAaddr), .sel(regDest));  // open: in1
  Priority_Encoder #(.select(2)) priority_encoder_1 (
    .in0(1'b1), .in1(comparator_1_gt), .in2(jsr), .out(priority_encoder_1_out));  // open: in3, gs, en_out, en_in
  Multiplexer #(.width(16), .enable("false")) multiplexer_3 (
    .in0(SPnext), .in1(subtractor_2_out), .out(setSPregOut), .sel(jsr));
  // Probe on priority_encoder_1_out
  // Probe on setPCregOut
  Multiplexer #(.select(2), .width(16), .enable("false")) multiplexer_4 (
    .in0(PCnext), .in1(ifxOut), .in2(valB), .out(setPCregOut), .sel(priority_encoder_1_out));  // open: in3
  Comparator #(.width(4), .mode("unsigned")) comparator_4 (
    .a(\reg ), .b(4'b1010), .gt(comparator_4_gt), .lt(comparator_4_lt));  // open: eq
  or or_1 (or_1_out, comparator_4_gt, comparator_4_lt);
  Register #(.width(16)) register_1 (.D(setSPregOut), .en(load), .Q(register_1_q), .clk(CLK_t), .clr(RST_t));
  assign SPOut = or_1_out ? register_1_q : 16'bz;  // Controlled_Buffer controlled_buffer_1
  // Probe on ramS
  // Probe on regS
  Comparator #(.width(4), .mode("unsigned")) comparator_5 (
    .a(\reg ), .b(4'b1001), .gt(comparator_5_gt), .lt(comparator_5_lt));  // open: eq
  Multiplexer #(.width(16)) multiplexer_5 (.in0(setSPregOut), .in1(setAaddr), .out(address), .sel(ramS), .en(ramW_t));
  Multiplexer #(.width(16)) multiplexer_6 (.in0(PCnext), .in1(setAramOut), .out(ramOut), .sel(ramS), .en(ramW_t));
  // Probe on regSel
  Multiplexer #(.select(2), .width(4)) multiplexer_7 (
    .in0(4'b1000), .in1(4'b1001), .in2(setAregSel), .in3(4'b1010), .out(regSel), .sel(regS), .en(regW_t));
  Multiplexer #(.select(2), .width(16)) multiplexer_8 (
    .in0(setSPregOut), .in1(setPCregOut), .in2(setAregOut), .in3(overflow), .out(regOut), .sel(regS),
    .en(regW_t));
  // Probe on regOut
  assign PCOut = or_2_out ? register_2_q : 16'bz;  // Controlled_Buffer controlled_buffer_2
  or or_2 (or_2_out, comparator_5_gt, comparator_5_lt);
  Register #(.width(16)) register_2 (.D(setPCregOut), .en(load), .Q(register_2_q), .clk(CLK_t), .clr(RST_t));
  ROM #(.addrWidth(7), .dataWidth(6)) rom_1 (
    .addr({op, regDest, phase}), .data({regW_t, regS, ramW_t, ramS, done}));  // open: sel
  or or_3 (CLK_t, button_1_out, CLK);
  Button button_1 (.out(button_1_out));
  and and_2 (ramW, load, ramW_t);
  and and_3 (regW, regW_t, load);
  Counter #(.width(2), .max('h3), .ongoal("stay")) counter_1 (
    .count(load), .Q(phase), .clk(CLK_t), .clr(RST_t));  // open: load, D, carry
  or or_4 (RST_t, RST, ~load);  // OR_Gate

  // Other names for the same wires on the sheet: addr[15:0] = address; regIn[3:0] = \reg ;
  //   setOregOut[15:0] = overflow

  // Notes on the sheet:
  //   contents of rom_1 (hex, n*v repeats v):
  //   4*0 24 28 1 0 6 1 0 0 30 1 0 0 3e 1 0 0 30 38 1 0 3e 1 0 0 30 38 1 0 3e 1 0 0 30 38 1 0 3e 1 0 0 30
  //   38 1 0 6 1 0 0 30 1 0 0 3e 1 0 0 30 38 1 0 3e 1 0 0 30 38 1 0 6 1 0 0 30 1 0 0 6 1 0 0 30 1 0 0 6 1
  //   0 0 30 1 0 0 28 1 0 0 28 1 0 0 28 1 0 0 28 1 0 0 28 1 0 0 28 1 0 0 28 1 0 0 28 1
endmodule

module jsr (
  input  [15:0] Input_B,
  output [15:0] PCout
);


  assign PCout = Input_B;
endmodule

// reg put
module reg_data_put (
  input  [3:0] regSel,
  input  [15:0] Data_In,
  input  load,
  output [15:0] A,
  output Awr,
  output [15:0] C,
  output Cwr,
  output [15:0] Y,
  output Ywr,
  output [15:0] I,
  output Iwr,
  output [15:0] SP,
  output SPwr,
  output [15:0] O,
  output Owr,
  output [15:0] B,
  output Bwr,
  output [15:0] X,
  output Cwr_2,
  output [15:0] Z,
  output Zwr,
  output [15:0] J,
  output Jwr,
  output [15:0] PC,
  output PCwr
);

  Decoder #(.select(4)) decoder_1 (
    .out0(Awr), .out1(Bwr), .out2(Cwr), .out3(Cwr_2), .out4(Ywr), .out5(Zwr), .out6(Iwr), .out7(Jwr),
    .out8(SPwr), .out9(PCwr), .out10(Owr), .sel(regSel), .en(load));  // open: out11, out12, out13, out14, out15
  Demultiplexer #(.select(4), .width(16)) demultiplexer_1 (
    .out0(A), .out1(B), .out2(C), .out3(X), .out4(Y), .out5(Z), .out6(I), .out7(J), .out8(SP), .out9(PC),
    .out10(O), .in(Data_In), .sel(regSel), .en(load));  // open: out11, out12, out13, out14, out15
endmodule

module control (
  input  DFready,
  input  EXready,
  input  CLK,
  input  RST,
  output DF,
  output EX,
  output IF
);

  wire counter_1_carry, decoder_1_out3, or_1_out, or_3_out;
  wire [1:0] counter_1_q;

  or or_1 (or_1_out, DFready, IF, EXready);
  // OR_Gate or_2 has open pins: in0=counter_1_carry, in1=or_3_out, out=open
  Counter #(.width(2), .max('h2)) counter_1 (
    .count(or_1_out), .Q(counter_1_q), .carry(counter_1_carry), .clk(CLK), .clr(or_3_out));  // open: load, D
  or or_3 (or_3_out, RST, decoder_1_out3);
  Decoder #(.select(2), .enable("false")) decoder_1 (
    .out0(IF), .out1(DF), .out2(EX), .out3(decoder_1_out3), .sel(counter_1_q));
endmodule
